# Fritzing sketch Traverser_v0.2 (saved by Fritzing 0.9.3b)
stripboards: 1

parts:
  R1 = Resistor [tolerance=±5% resistance=220 package=THT]
  R3 = Resistor [tolerance=±5% resistance=1.5k package=THT]
  LED2 = LED - 3mm [color="Yellow (595nm)" package="3 mm [THT]"]
  LED3 = LED - 3mm [color="Green (570nm)" package="3 mm [THT]"]
  R4 = Resistor [tolerance=±5% resistance=330 package=THT]
  LED4 = LED - 3mm [color="White (4500K)" package="3 mm [THT]"]
  IC3 = ULN2803A [package=THT]
  R7 = Resistor [tolerance=±5% resistance=4.7k package=THT]
  R8 = Resistor [tolerance=±5% resistance=4.7k package=THT]
  R9 = Resistor [tolerance=±5% resistance=4.7k package=THT]
  R10 = Resistor [tolerance=±5% resistance=100 package=THT]
  R11 = Resistor [tolerance=±5% resistance=100 package=THT]
  R12 = Resistor [tolerance=±5% resistance=100 package=THT]
  R13 = Resistor [tolerance=±5% resistance=220 package=THT]
  R14 = Resistor [tolerance=±5% resistance=220 package=THT]
  R15 = Resistor [tolerance=±5% resistance=220 package=THT]
  J2 = female pin header, 8 pins [form="♀ (female)"]
  J3 = female pin header, 8 pins [form="♀ (female)"]
  J4 = female pin header, 5 pins [form="♀ (female)"]
  J5 = female pin header, 2 pins [form="♀ (female)"]
  J6 = female pin header, 5 pins [form="♀ (female)"]  # not connected
  J7 = female pin header, 8 pins [form="♀ (female)"]  # not connected

nets:
  N1: R1.Pin_0, R3.Pin_0, LED4.anode, IC3.0V, J2.pin7, J3.pin6
  N2: R1.Pin_1, LED3.anode
  N3: R3.Pin_1, LED2.anode
  N4: LED2.cathode, IC3.Out_8, R11.Pin_1, J3.pin5
  N5: LED3.cathode, R4.Pin_1, IC3.In_6, IC3.In_7, IC3.In_8, R7.Pin_1, R8.Pin_1, R9.Pin_1, J2.pin2, J2.pin6, J3.pin1, J3.pin3, J3.pin8, J4.pin3, J5.pin2
  N6: R4.Pin_0, LED4.cathode
  N7: IC3.Out_7, R10.Pin_1
  N8: IC3.Out_6, R12.Pin_1
  N9: R7.Pin_0, J2.pin4
  N10: R8.Pin_0, J2.pin8
  N11: R9.Pin_0, J4.pin5
  N12: R10.Pin_0, J2.pin1
  N13: R11.Pin_0, J4.pin2
  N14: R12.Pin_0, J2.pin5
  N15: R13.Pin_0, J5.pin1
  N16: R13.Pin_1, R15.Pin_0, R15.Pin_1, J3.pin2
  N17: R14.Pin_0, R14.Pin_1, J3.pin4

notes:
  Arduino NANO
  GND
  5V
  DC - DC
  24V
  J5
  MISO
  MOSI
  SDA(SS)
  RST
  SCK
  pos ACK
  trav pos
  srv decpl
  green
  red
  3V3
  pos 1
  pos 2
  pos 3
  pos 4
  ir decpl
  ir trav
  ir start
  ir start tx
  ir decpl tx
  ir trav tx
  J1
  yellow
  J2
  J3
  J4
  J6
  1
  Traverser control pcb ver 0.2 aug 2016
